// Logisim project cpu.circ as structural Verilog: 11 circuits, main circuit main
module NPC (
  input  [31:0] Pc,
  input  isZero,
  input  [15:0] imm,
  input  NPCOp,
  output [31:0] Npc
);

  wire and_1_out;
  wire [31:0] adder_1_out, adder_2_out, bit_extender_1_out, shifter_1_out;

  assign bit_extender_1_out = {{16{imm[15]}}, imm};  // Bit_Extender bit_extender_1
  Shifter #(.width(32)) shifter_1 (.in(bit_extender_1_out), .\dist (5'b00010), .out(shifter_1_out));
  Adder #(.width(32)) adder_1 (.a(Pc), .b(32'h4), .out(adder_1_out));  // open: cin, cout
  and and_1 (and_1_out, isZero, NPCOp);
  Adder #(.width(32)) adder_2 (.a(adder_1_out), .b(shifter_1_out), .out(adder_2_out));  // open: cin, cout
  Multiplexer #(.width(32)) multiplexer_1 (
    .in0(adder_1_out), .in1(adder_2_out), .out(Npc), .sel(and_1_out));  // open: en
endmodule

module IFU (
  input  Reset,
  input  isZero,
  input  [15:0] imm,
  input  NPCOp,
  output [31:0] Instr,
  output [31:0] pc
);

  wire clock_1_out;
  wire [11:0] subtractor_1_out;
  wire [31:0] Npc, Pc_q;

  Clock clock_1 (.out(clock_1_out));
  Register #(.width(32)) u_Pc (.D(Npc), .Q(Pc_q), .clk(clock_1_out), .clr(Reset));  // open: en
  NPC npc_1 (.Pc(Pc_q), .isZero(isZero), .imm(imm), .NPCOp(NPCOp), .Npc(Npc));
  Adder #(.width(32)) adder_1 (.a(Pc_q), .b(32'h3000), .out(pc));  // open: cin, cout
  // Probe on subtractor_1_out
  Subtractor #(.width(12)) subtractor_1 (.a(pc[13:2]), .b(12'hc00), .out(subtractor_1_out));  // open: bin, bout
  ROM #(.addrWidth(12), .dataWidth(32)) rom_1 (.addr(subtractor_1_out), .data(Instr));  // open: sel

  // Notes on the sheet:
  //   contents of rom_1 (hex, n*v repeats v):
  //   3c1f179e 37ffebaf 3c1e23a8 37de012b 3c1de335 37bd4f73 3c1cf06f 379c8f15 3c1bf031 377bd0cb 3c1a81ce
  //   375a0e1d 3c1963cf 3739e9d5 3c18c501 37182a78 3c179a6e 36f71eca 3c161d6a 36d6efb9 3c1508ec 36b547b8
  //   3c14bc8d 36948bc2 3c132bc4 367364af 3c12d9ec 36523a92 3c114523 3631a238 3c104aad 36101cb2 3c0fdc99
  //   35ef81bb 3c0e21ca 35cea978 3c0db9e2 35ad5e64 3c0c754d 358c2f8a 3c0b6038 356bcbc7 3c0a8bc7 354ae707
  //   3c098cfc 3529f372 3c086484 3508d57f 3c07c324 34e76a08 3c066240 34c61be1 3c057446 34a5e0f7 3c041afa
  //   3484fbff 3c038a8d 346310e1 3c02c318 34427388 3c010ad6 3421730c 352ed84d 13660083 8d560000 34110001
  //   02318820 10000001 105dffd0 34bd2acb 007d9020 34ef8bd0 34029eb4 8e980000 34110001 02318820 10000001
  //   132fffe5 ac0915f4 00e0c822 34110001 02318820 10000001 11e3ffd2 01259822 02863822 13f501e4 ac1d2494
  //   0212b822 13f00243 01538020 11ba020d 8c1215f4 13340222 118e0056 0112b022 1087006e 03eeb822 8c1a15f4
  //   01067822 019bc822 0070b820 03129020 005ff022 8c1615f4 136a0240 138a01e1 029d6822 35dd2e20 02a50820
  //   ac0b2b48 8c0815f4 346f1902 34110001 02318820 10000001 13deffe2 8c002494 361544b4 02609020 366cfbd6
  //   011e1020 ac0c1f70 0376c020 02522820 1281005a 34110001 02318820 10000001 1266ffa6 02dfe020 13dd0151
  //   ac062d10 116e020a 8c0b15f4 8c0d1f70 12500129 03ab2820 11dd00d6 12f3007b 10ce0081 34aa9660 02925022
  //   8c0215f4 34cc1fd8 8c0615f4 10be015d ac020ad0 ac1710ec 8c0d15f4 35c0df25 8c1c2b48 36b4e1ce 035b0820
  //   016c3022 34110001 02318820 10000001 12b6ffca ac0e1388 0124e820 34110001 02318820 10000001 115cffab
  //   03fd0020 0061b822 03987822 016a8022 0187e820 8c152d10 8c052494 12cc00a7 0363b020 03c25020 029d7822
  //   014d9822 03d3e820 ac1501d8 ac04254c 00bad820 03bc0022 35a605ab 34110001 02318820 10000001 12e8ffbc
  //   11500130 13f20087 0380e822 121c01d3 02ad7820 ac0e0c28 01797822 ac1e12b8 8c021f70 8c1e2d10 34110001
  //   02318820 10000001 110afffb 03a86022 3684b60a 03b78022 01fd6020 34110001 02318820 10000001 1319ffd3
  //   0101e822 36cb72a3 8c182b48 038fc020 10a10152 1141000b ac191eb0 0254f820 030fb022 ac0d0548 0270a820
  //   8c1501d8 12900166 03013822 367e5fc5 0269c020 014dd020 02123820 35122cf0 02590020 ac0725bc 13950102
  //   8c030c28 8c180548 009b9022 ac1e26d8 8c062b48 34110001 02318820 10000001 10edff52 ac041188 ac1e29ec
  //   366c868c 378a7c9d 34110001 02318820 10000001 13c2ff10 34110001 02318820 10000001 11f5ff55 8c042d10
  //   0064b822 37bf3393 10500086 00c77020 35f0a559 368cad81 349c50d6 8c0615f4 133b00ea 12bc0056 02743022
  //   369505bf ac001d7c 00cc1820 8c1e2d10 02588022 11d80197 02000022 03699020 039b3822 03f43822 8c0a2d10
  //   01f6e822 8c1f2494 34110001 02318820 10000001 1166ff1f 034ea820 13740083 007bb822 110c00c3 8c1610ec
  //   0374a820 ac0e2724 ac0409c0 02866022 034a9020 36deab86 36a2e3ba 34110001 02318820 10000001 124aff38
  //   03184022 026ed020 34110001 02318820 10000001 120bff22 125700b7 ac132f10 8c172d10 36d4060d 34db299a
  //   01402022 8c020c28 ac1e2254 ac1d0f8c 34110001 02318820 10000001 10c6ffb9 13450080 02f07020 ac152788
  //   376add18 013ee022 019db020 36496201 34110001 02318820 10000001 12aeff62 00d69822 ad122cbc 8c001188
  //   3738b3a5 358d108e 370df9a8 8c0229ec 8c001d7c 8c050f8c 344ae3e7 02f24820 ac0b2704 0272d822 34110001
  //   02318820 10000001 137cfea9 00ae3820 34110001 02318820 10000001 131fffc6 00e4b822 34110001 02318820
  //   10000001 121dff8b ac1a0c88 02b98020 8c0715f4 8c1610ec ac080d94 8c0b01d8 34110001 02318820 10000001
  //   1312fed3 3687ac75 0100a820 353f2b3b 00324020 34110001 02318820 10000001 12cefff4 34110001 02318820
  //   10000001 12f2ff40 00a36822 01273822 358becd5 350fc9ef 11ef003d ac162df8 8c161f70 01b5e020 02caa022
  //   139f00a2 030f9020 0008a022 01f0b020 000b5820 03a70020 0325c820 341e29cd ac051888 139b008b 34110001
  //   02318820 10000001 1260ff8d 34110001 02318820 10000001 10c0fea9 ac010ef8 35b35da6 ac000828 03fbc822
  //   8c04254c 8c121388 00d5b022 34110001 02318820 10000001 13afffaf 34110001 02318820 10000001 1309fe86
  //   11a80109 8c1f10ec 8c0c0ef8 ac182f74 8fd9d80b 8c0309c0 10df005c ac090b68 01a86022 35cb530c ac190864
  //   13720081 ac1d0ff4 8c040f8c 34110001 02318820 10000001 13ecfe74 36befc0d 03720822 8c1d2788 8c091d7c
  //   8c1b2df8 8c0112b8 34110001 02318820 1000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
endmodule

module GRF (
  input  reset,
  input  Wr,
  input  [4:0] Rs,
  input  [4:0] Rt,
  input  [4:0] Wt,
  input  [31:0] WD,
  output [31:0] RD1,
  output [31:0] RD2
);

  wire clock_1_out, w1, w2, w3, w4, w5, w6, w7, w8, w9, w10, w11, w12, w13, w14, w15, w16, w17, w18, w19,
       w20, w21, w22, w23, w24, w25, w26, w27, w28, w29, w30, w31;
  wire [31:0] _1, _2, _3, _4, _5, _6, _7, _8, _9, _10, _11, _12, _13, _14, _15, _16, _17, _18, _19, _20, _21,
       _22, _23, _24, _25, _26, _27, _28, _29, _30, _31;

  Clock clock_1 (.out(clock_1_out));
  Multiplexer #(.select(5), .width(32)) multiplexer_1 (
    .in0({32{1'b0}}), .in1(_1), .in2(_2), .in3(_3), .in4(_4), .in5(_5), .in6(_6), .in7(_7), .in8(_8),
    .in9(_9), .in10(_10), .in11(_11), .in12(_12), .in13(_13), .in14(_14), .in15(_15), .in16(_16), .in17(_17),
    .in18(_18), .in19(_19), .in20(_20), .in21(_21), .in22(_22), .in23(_23), .in24(_24), .in25(_25),
    .in26(_26), .in27(_27), .in28(_28), .in29(_29), .in30(_30), .in31(_31), .out(RD1), .sel(Rs));  // open: en
  Register #(.width(32)) register_1 (.D(WD), .en(w1), .Q(_1), .clk(clock_1_out), .clr(reset));
  Register #(.width(32)) register_2 (.D(WD), .en(w8), .Q(_8), .clk(clock_1_out), .clr(reset));
  Register #(.width(32)) register_3 (.D(WD), .en(w9), .Q(_9), .clk(clock_1_out), .clr(reset));
  Register #(.width(32)) register_4 (.D(WD), .en(w17), .Q(_17), .clk(clock_1_out), .clr(reset));
  Register #(.width(32)) register_5 (.D(WD), .en(w16), .Q(_16), .clk(clock_1_out), .clr(reset));
  Register #(.width(32)) register_6 (.D(WD), .en(w24), .Q(_24), .clk(clock_1_out), .clr(reset));
  Register #(.width(32)) register_7 (.D(WD), .en(w25), .Q(_25), .clk(clock_1_out), .clr(reset));
  Register #(.width(32)) register_8 (.D(WD), .en(w2), .Q(_2), .clk(clock_1_out), .clr(reset));
  Register #(.width(32)) register_9 (.D(WD), .en(w10), .Q(_10), .clk(clock_1_out), .clr(reset));
  Register #(.width(32)) register_10 (.D(WD), .en(w18), .Q(_18), .clk(clock_1_out), .clr(reset));
  Register #(.width(32)) register_11 (.D(WD), .en(w26), .Q(_26), .clk(clock_1_out), .clr(reset));
  Multiplexer #(.select(5), .width(32)) multiplexer_2 (
    .in0({32{1'b0}}), .in1(_1), .in2(_2), .in3(_3), .in4(_4), .in5(_5), .in6(_6), .in7(_7), .in8(_8),
    .in9(_9), .in10(_10), .in11(_11), .in12(_12), .in13(_13), .in14(_14), .in15(_15), .in16(_16), .in17(_17),
    .in18(_18), .in19(_19), .in20(_20), .in21(_21), .in22(_22), .in23(_23), .in24(_24), .in25(_25),
    .in26(_26), .in27(_27), .in28(_28), .in29(_29), .in30(_30), .in31(_31), .out(RD2), .sel(Rt));  // open: en
  Register #(.width(32)) register_12 (.D(WD), .en(w3), .Q(_3), .clk(clock_1_out), .clr(reset));
  Register #(.width(32)) register_13 (.D(WD), .en(w11), .Q(_11), .clk(clock_1_out), .clr(reset));
  Register #(.width(32)) register_14 (.D(WD), .en(w19), .Q(_19), .clk(clock_1_out), .clr(reset));
  Register #(.width(32)) register_15 (.D(WD), .en(w27), .Q(_27), .clk(clock_1_out), .clr(reset));
  Register #(.width(32)) register_16 (.D(WD), .en(w4), .Q(_4), .clk(clock_1_out), .clr(reset));
  Register #(.width(32)) register_17 (.D(WD), .en(w12), .Q(_12), .clk(clock_1_out), .clr(reset));
  Register #(.width(32)) register_18 (.D(WD), .en(w20), .Q(_20), .clk(clock_1_out), .clr(reset));
  Register #(.width(32)) register_19 (.D(WD), .en(w28), .Q(_28), .clk(clock_1_out), .clr(reset));
  Demultiplexer #(.select(5)) demultiplexer_1 (
    .out1(w1), .out2(w2), .out3(w3), .out4(w4), .out5(w5), .out6(w6), .out7(w7), .out8(w8), .out9(w9),
    .out10(w10), .out11(w11), .out12(w12), .out13(w13), .out14(w14), .out15(w15), .out16(w16), .out17(w17),
    .out18(w18), .out19(w19), .out20(w20), .out21(w21), .out22(w22), .out23(w23), .out24(w24), .out25(w25),
    .out26(w26), .out27(w27), .out28(w28), .out29(w29), .out30(w30), .out31(w31), .in(Wr), .sel(Wt));  // open: out0, en
  Register #(.width(32)) register_20 (.D(WD), .en(w5), .Q(_5), .clk(clock_1_out), .clr(reset));
  Register #(.width(32)) register_21 (.D(WD), .en(w13), .Q(_13), .clk(clock_1_out), .clr(reset));
  Register #(.width(32)) register_22 (.D(WD), .en(w21), .Q(_21), .clk(clock_1_out), .clr(reset));
  Register #(.width(32)) register_23 (.D(WD), .en(w29), .Q(_29), .clk(clock_1_out), .clr(reset));
  Register #(.width(32)) register_24 (.D(WD), .en(w6), .Q(_6), .clk(clock_1_out), .clr(reset));
  Register #(.width(32)) register_25 (.D(WD), .en(w14), .Q(_14), .clk(clock_1_out), .clr(reset));
  Register #(.width(32)) register_26 (.D(WD), .en(w22), .Q(_22), .clk(clock_1_out), .clr(reset));
  Register #(.width(32)) register_27 (.D(WD), .en(w30), .Q(_30), .clk(clock_1_out), .clr(reset));
  Register #(.width(32)) register_28 (.D(WD), .en(w7), .Q(_7), .clk(clock_1_out), .clr(reset));
  Register #(.width(32)) register_29 (.D(WD), .en(w15), .Q(_15), .clk(clock_1_out), .clr(reset));
  Register #(.width(32)) register_30 (.D(WD), .en(w23), .Q(_23), .clk(clock_1_out), .clr(reset));
  Register #(.width(32)) register_31 (.D(WD), .en(w31), .Q(_31), .clk(clock_1_out), .clr(reset));

  // Other names for the same wires on the sheet: A1[4:0] = Rs; A2[4:0] = Rt; A3[4:0] = Wt; w[31:0] = WD
endmodule

module ALU (
  input  [31:0] A,
  input  [31:0] B,
  input  [1:0] ALUOp,
  output [31:0] C,
  output isZero
);

  wire [31:0] adder_1_out, or_1_out, subtractor_1_out;

  Adder #(.width(32)) adder_1 (.a(A), .b(B), .out(adder_1_out));  // open: cin, cout
  Subtractor #(.width(32)) subtractor_1 (.a(A), .b(B), .out(subtractor_1_out));  // open: bin, bout
  assign or_1_out = A | B;  // OR_Gate or_1, 32 bits wide
  Comparator #(.width(32)) comparator_1 (.a(A), .b(B), .eq(isZero));  // open: gt, lt
  Multiplexer #(.select(2), .width(32)) multiplexer_1 (
    .in0(adder_1_out), .in1(subtractor_1_out), .in2(or_1_out), .in3({32{1'b0}}), .out(C), .sel(ALUOp));  // open: en
endmodule

module DM (
  input  [31:0] Ad,
  input  [31:0] Wd,
  input  Reset,
  input  Wr,
  output [31:0] Rd
);

  wire clock_1_out;

  Clock clock_1 (.out(clock_1_out));
  RAM #(.addrWidth(12), .dataWidth(32), .bus("separate")) ram_1 (
    .addr(Ad[13:2]), .din(Wd), .data(Rd), .str(Wr), .clk(clock_1_out), .clr(Reset));  // open: sel, ld
endmodule

module EXT (
  input  [15:0] imm,
  input  [1:0] EXTOp,
  output [31:0] out
);

  wire [31:0] bit_extender_1_out, bit_extender_2_out;

  assign bit_extender_1_out = {{16{1'b0}}, imm};  // Bit_Extender bit_extender_1
  assign bit_extender_2_out = {{16{imm[15]}}, imm};  // Bit_Extender bit_extender_2
  Multiplexer #(.select(2), .width(32)) multiplexer_1 (
    .in0(bit_extender_1_out), .in1(bit_extender_2_out), .in2({imm, {16{1'b0}}}), .in3({32{1'b0}}), .out(out),
    .sel(EXTOp));  // open: en
endmodule

module OP (
  input  [5:0] Op,
  input  [5:0] funct,
  output ori,
  output \and ,
  output lw,
  output sub,
  output sw,
  output beq,
  output lui
);

  wire not_1_out, not_2_out, not_3_out, not_4_out, not_5_out, not_6_out, not_7_out, not_8_out, not_9_out,
       not_10_out, not_11_out, not_12_out, R;

  not not_1 (not_1_out, Op[0]);
  not not_2 (not_2_out, Op[1]);
  not not_3 (not_3_out, Op[3]);
  not not_4 (not_4_out, Op[2]);
  not not_5 (not_5_out, Op[5]);
  not not_6 (not_6_out, Op[4]);
  and and_1 (ori, not_5_out, not_6_out, Op[3], Op[2], not_2_out, Op[0]);
  and and_2 (lw, Op[5], not_6_out, not_3_out, not_4_out, Op[1], Op[0]);
  and and_3 (sw, Op[5], not_6_out, Op[3], not_4_out, Op[1], Op[0]);
  and and_4 (beq, not_5_out, not_6_out, not_3_out, Op[2], not_2_out, not_1_out);
  and and_5 (lui, not_5_out, not_6_out, Op[3], Op[2], Op[1], Op[0]);
  and and_6 (R, not_5_out, not_6_out, not_3_out, not_4_out, not_2_out, not_1_out);
  not not_7 (not_7_out, funct[0]);
  not not_8 (not_8_out, funct[1]);
  not not_9 (not_9_out, funct[2]);
  not not_10 (not_10_out, funct[4]);
  not not_11 (not_11_out, funct[3]);
  not not_12 (not_12_out, funct[5]);
  and and_7 (\and , funct[5], not_10_out, not_11_out, not_9_out, not_8_out, not_7_out, R);
  and and_8 (sub, funct[5], not_10_out, not_11_out, not_9_out, funct[1], not_7_out, R);
endmodule

module CTL (
  input  add,
  input  sub,
  input  ori,
  input  lw,
  input  sw,
  input  beq,
  input  lui,
  output NPCOp,
  output [1:0] EXTOp,
  output [1:0] ALUOp,
  output GRFWr,
  output DMWr,
  output M1Sel,
  output [1:0] M2Sel,
  output M3Sel
);

  wire not_1_out, not_2_out, not_3_out, not_4_out, not_5_out, not_6_out, not_7_out;

  not not_1 (not_1_out, add);
  not not_2 (not_2_out, ori);
  not not_3 (not_3_out, sub);
  not not_4 (not_4_out, lw);
  not not_5 (not_5_out, sw);
  not not_6 (not_6_out, lui);
  not not_7 (not_7_out, beq);
  or or_1 (EXTOp[0], sw, lw);
  and and_1 (GRFWr, not_5_out, not_7_out);
  or or_2 (M1Sel, add, sub);
  or or_3 (M3Sel, sw, lw, ori);

  assign ALUOp = {ori, sub};
  assign DMWr = sw;
  assign EXTOp[1] = lui;
  assign M2Sel = {lui, lw};
  assign NPCOp = beq;
endmodule

module Controller (
  input  [5:0] Opcode,
  input  [5:0] Funct,
  output NPCOp,
  output [1:0] EXTOp,
  output [1:0] ALUOp,
  output GRFWr,
  output DMWr,
  output M1Sel,
  output [1:0] M2Sel,
  output M3Sel
);

  wire op_1_and, op_1_beq, op_1_lui, op_1_lw, op_1_ori, op_1_sub, op_1_sw;

  OP op_1 (
    .Op(Opcode), .funct(Funct), .ori(op_1_ori), .\and (op_1_and), .lw(op_1_lw), .sub(op_1_sub), .sw(op_1_sw),
    .beq(op_1_beq), .lui(op_1_lui));
  CTL ctl_1 (
    .NPCOp(NPCOp), .EXTOp(EXTOp), .ALUOp(ALUOp), .GRFWr(GRFWr), .DMWr(DMWr), .M1Sel(M1Sel), .M2Sel(M2Sel),
    .M3Sel(M3Sel), .add(op_1_and), .sub(op_1_sub), .ori(op_1_ori), .lw(op_1_lw), .sw(op_1_sw),
    .beq(op_1_beq), .lui(op_1_lui));
endmodule

module main (
  input  reset,
  output [31:0] Instr,
  output [31:0] pc,
  output RegWrite,
  output [4:0] RegAddr,
  output [31:0] RegData,
  output MemWrite,
  output [31:0] MemAddr,
  output [31:0] MemData
);

  wire controller_1_m1sel, controller_1_m3sel, isZero, NPCOp;
  wire [1:0] controller_1_aluop, controller_1_m2sel, EXTOp;
  wire [4:0] splitter_1_rd, splitter_1_rs, splitter_1_rt;
  wire [5:0] splitter_1_funct, splitter_1_opcode;
  wire [15:0] splitter_1_imm;
  wire [31:0] DMOut, EXTOut, grf_1_rd1, multiplexer_3_out;

  IFU ifu_1 (.Reset(reset), .Instr(Instr), .isZero(isZero), .imm(splitter_1_imm), .pc(pc), .NPCOp(NPCOp));
  Splitter splitter_1 (
    .Instr(Instr), .Funct(splitter_1_funct), .Imm(splitter_1_imm), .Rd(splitter_1_rd), .Rt(splitter_1_rt),
    .Rs(splitter_1_rs), .Opcode(splitter_1_opcode));
  Controller controller_1 (
    .Opcode(splitter_1_opcode), .Funct(splitter_1_funct), .NPCOp(NPCOp), .EXTOp(EXTOp),
    .ALUOp(controller_1_aluop), .GRFWr(RegWrite), .DMWr(MemWrite), .M1Sel(controller_1_m1sel),
    .M2Sel(controller_1_m2sel), .M3Sel(controller_1_m3sel));
  Multiplexer #(.width(5)) multiplexer_1 (
    .in0(splitter_1_rt), .in1(splitter_1_rd), .out(RegAddr), .sel(controller_1_m1sel));  // open: en
  Multiplexer #(.select(2), .width(32)) multiplexer_2 (
    .in0(MemAddr), .in1(DMOut), .in2(EXTOut), .in3({32{1'b0}}), .out(RegData), .sel(controller_1_m2sel));  // open: en
  EXT ext_1 (.imm(splitter_1_imm), .EXTOp(EXTOp), .out(EXTOut));
  GRF grf_1 (
    .Rs(splitter_1_rs), .Rt(splitter_1_rt), .Wt(RegAddr), .WD(RegData), .RD1(grf_1_rd1), .RD2(MemData),
    .reset(reset), .Wr(RegWrite));
  Multiplexer #(.width(32)) multiplexer_3 (
    .in0(MemData), .in1(EXTOut), .out(multiplexer_3_out), .sel(controller_1_m3sel));  // open: en
  ALU alu_1 (.A(grf_1_rd1), .B(multiplexer_3_out), .ALUOp(controller_1_aluop), .C(MemAddr), .isZero(isZero));
  DM dm_1 (.Ad(MemAddr), .Wd(MemData), .Reset(reset), .Wr(MemWrite), .Rd(DMOut));

  // Other names for the same wires on the sheet: ALUOut[31:0] = MemAddr
endmodule

module Splitter (
  input  [31:0] Instr,
  output [5:0] Funct,
  output [15:0] Imm,
  output [4:0] Rd,
  output [4:0] Rt,
  output [4:0] Rs,
  output [5:0] Opcode
);


  assign Funct = Instr[5:0];
  assign Imm = Instr[15:0];
  assign Opcode = Instr[31:26];
  assign Rd = Instr[15:11];
  assign Rs = Instr[25:21];
  assign Rt = Instr[20:16];
endmodule
