// Logisim project cpu.circ as structural Verilog: 11 circuits, main circuit main
module NPC (
  input  [31:0] Pc,
  input  isZero,
  input  [15:0] imm,
  input  NPCOp,
  output [31:0] Npc
);

  wire and_1_out;
  wire [31:0] adder_1_out, adder_2_out, bit_extender_1_out, shifter_1_out;

  assign bit_extender_1_out = {{16{imm[15]}}, imm};  // Bit_Extender bit_extender_1
  Shifter #(.width(32)) shifter_1 (.in(bit_extender_1_out), .\dist (5'b00010), .out(shifter_1_out));
  Adder #(.width(32)) adder_1 (.a(Pc), .b(32'h4), .out(adder_1_out));  // open: cin, cout
  and and_1 (and_1_out, isZero, NPCOp);
  Adder #(.width(32)) adder_2 (.a(adder_1_out), .b(shifter_1_out), .out(adder_2_out));  // open: cin, cout
  Multiplexer #(.width(32)) multiplexer_1 (
    .in0(adder_1_out), .in1(adder_2_out), .out(Npc), .sel(and_1_out));  // open: en
endmodule

module IFU (
  input  Reset,
  input  isZero,
  input  [15:0] imm,
  input  NPCOp,
  output [31:0] Instr,
  output [31:0] pc
);

  wire clock_1_out;
  wire [11:0] subtractor_1_out;
  wire [31:0] Npc, Pc_q;

  Clock clock_1 (.out(clock_1_out));
  Register #(.width(32)) u_Pc (.D(Npc), .Q(Pc_q), .clk(clock_1_out), .clr(Reset));  // open: en
  NPC npc_1 (.Pc(Pc_q), .isZero(isZero), .imm(imm), .NPCOp(NPCOp), .Npc(Npc));
  Adder #(.width(32)) adder_1 (.a(Pc_q), .b(32'h3000), .out(pc));  // open: cin, cout
  // Probe on subtractor_1_out
  Subtractor #(.width(12)) subtractor_1 (.a(pc[13:2]), .b(12'hc00), .out(subtractor_1_out));  // open: bin, bout
  ROM #(.addrWidth(12), .dataWidth(32)) rom_1 (.addr(subtractor_1_out), .data(Instr));  // open: sel

  // Notes on the sheet:
  //   contents of rom_1 (hex, n*v repeats v):
  //   3c1fe59b 37ff72e3 3c1e618d 37de7a63 3c1d2549 37bdc3d6 3c1ce3a2 379c6e2f 3c1b36a6 377b25d5 3c1adf9d
  //   375ad72f 3c19f279 3739cd4c 3c1851e4 3718610f 3c17d0e0 36f711cd 3c166486 36d6bcad 3c156378 36b5b80d
  //   3c1410f3 369401d6 3c135b29 3673bd2b 3c127a32 36528090 3c119402 3631dd1f 3c108264 36106edb 3c0f0c7a
  //   35ef1f19 3c0e509d 35ce9131 3c0dedff 35ad3b16 3c0c9174 358c5b1a 3c0b6cb6 356b2a70 3c0a8996 354a9bef
  //   3c0913e4 3529e866 3c088d7b 35085c3c 3c0774ef 34e7dcb1 3c06c5c1 34c617cd 3c05d9ec 34a5a0e0 3c0419bf
  //   34849a9e 3c030f40 3463a8fc 3c0220df 3442b504 3c01af3f 3421e96e ac1112ec 00b9a820 8c1612ec 34140001
  //   0014a022 10000001 1027ffcd ac0d2950 ac1719dc 8c1d2950 01d14020 ac0c00bc 02d00820 8c0e00bc 033f4820
  //   01159822 103900fe 03ebb822 0028f020 8c1a12ec ac16124c 13040196 10c501d7 3619e8c8 11880082 8c0d12ec
  //   02de3022 005e1020 02aaf820 ac150fc4 10b30078 37afeb14 37dc60d8 014d2020 351f2830 11880217 111a01ae
  //   ac011488 017df020 109d00c8 03efb020 36c8cf84 130001f0 018ef022 ac1c2a08 10190234 00bd7820 03562820
  //   132f014c 366d00db 357a9a97 8c03124c 37ebba64 00902020 8c152950 8c132950 00754820 8c0319dc 00585020
  //   03a6e020 0372a820 01752020 8c0a12ec 02722020 34140001 0014a022 10000001 1180ffbf 8c1c0fc4 8c1512ec
  //   12b301f9 03b73822 02e32020 00fe0022 34124089 03cbd022 0108f020 8c1512ec 03ef7022 37ca3bc8 34f279cc
  //   35fbda6f 8c172950 02c3a820 125601dd 35962381 8c0512ec 35f577e7 00898020 027e7822 ac160d0c 011cb820
  //   ac1a152c 01ba9020 34140001 0014a022 10000001 103dffd6 355623bd 01666022 8c08152c ac13277c 8c040fc4
  //   8c160d0c 037b9820 12040088 353c354a 35b73860 0273c822 03c61820 106f018d 3479ff35 02a25020 00350022
  //   0087d022 ac1b0cd4 ac0c1ba0 0039d022 ac151c60 364021c3 8c060fc4 ac112b60 00164820 8c0900bc ac1b2e48
  //   8c0b2b60 8c0f277c 8c072b60 8c1b152c 34140001 0014a022 10000001 10b5ffc4 ac1c0dd0 ac1f1d58 8c11277c
  //   35273aac 8c0c2b60 03d06020 36292d3e 13b00183 10d00078 36a9e012 131101ce 02e09020 8c030d0c ac172098
  //   0396e022 8c1f0dd0 8c1f12ec 365bdfb2 36dc5353 ac1f26ac 01def020 127c0079 038c3820 02427822 03ddf022
  //   10310025 34140001 0014a022 10000001 1218ff74 ac061214 137501c7 01358022 ac0422c8 376d8ab0 037da822
  //   8c000cd4 ac150200 ac0d10d8 13e90078 363d379f 8c150200 01080020 ac1c2a2c 009bb820 0068b020 34140001
  //   0014a022 10000001 10c6ff78 020de022 00e0b020 00e4a820 018f2820 ac0a0dd8 8c0326ac ac071664 34140001
  //   0014a022 10000001 1112ffee 8c190dd0 37e4256f 37d8b42b 032f2820 8c191488 8c172a2c 1042015b ac051918
  //   35bba513 35ba0969 357feece 02394822 34140001 0014a022 10000001 125dffaf 34070b70 355c1879 01f68020
  //   ac151c1c ac051c5c 032d6820 8c0812ec 032ef820 8c181488 011f0822 354bcb90 ac000fc4 13fc00fe 8c0f0fc4
  //   0033b822 8c0a0fc4 111a0029 ac03151c 02036822 02ac0022 3576773e 02d50820 01d33020 0343a820 00951020
  //   34140001 0014a022 10000001 1151ff61 3762d25b 34140001 0014a022 10000001 112fff99 024e0022 03371022
  //   8c170200 8c1c00bc 0309a822 02796020 ac1920b0 36a8d8e3 8c150cd4 0255e020 ac100b78 3421d71c ac060e10
  //   8c1b2950 00cab820 34140001 0014a022 10000001 1182ff5a 01aa6022 01510822 8c1f151c 01722022 02256822
  //   006c1820 12110058 ac101c9c 8c030fc4 ac1b0ab0 8c090cd4 376b4fa1 ac0f270c 8c0a1d58 34140001 0014a022
  //   10000001 10f9fec1 10bf0015 34b594d1 8c1e1664 ac112c24 ac132044 ac190904 00fc5820 3668badc ac160f30
  //   03879820 8c0b0e10 8c121664 373c6461 009a4020 8c1a1c9c 131500e5 8c1d2098 34120832 8c081488 01765020
  //   ac152478 034a4020 032eb022 131d004f 34140001 0014a022 10000001 1239ff63 8c07152c 3430e9a3 02b24022
  //   36b3fb2a 031f3022 02ca8022 11f5007c ac160804 01d37820 8c1a0cd4 ac0a04c8 10480038 34140001 0014a022
  //   10000001 105ffecf 01e1b822 34140001 0014a022 10000001 10f8fe7a ac1907b8 03b50020 ac1d07e4 ac0915f8
  //   02b72822 8c060fc4 359914ff 8c031c60 0009c022 027e6022 00ded022 007d9822 01c85020 ac081470 00f52820
  //   ac102124 34140001 0014a022 10000001 1371fe92 038c7822 134000ed 34e90ea1 00d0e820 02d1d822 008c6820
  //   34140001 0014a022 10000001 10d7fec4 35f1e92e 8c0610d8 ac182478 01ddf822 8c1d0fc4 00921020 34140001
  //   0014a022 10000001 10d1ff71 ac1f299c 34140001 0014a022 10000001 1157fec0 ac100ef4 8c1c20b0 02e7a820
  //   ac150c54 35ac6c31 01bde822 0195a820 03ff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
endmodule

module GRF (
  input  reset,
  input  Wr,
  input  [4:0] Rs,
  input  [4:0] Rt,
  input  [4:0] Wt,
  input  [31:0] WD,
  output [31:0] RD1,
  output [31:0] RD2
);

  wire clock_1_out, w1, w2, w3, w4, w5, w6, w7, w8, w9, w10, w11, w12, w13, w14, w15, w16, w17, w18, w19,
       w20, w21, w22, w23, w24, w25, w26, w27, w28, w29, w30, w31;
  wire [31:0] _1, _2, _3, _4, _5, _6, _7, _8, _9, _10, _11, _12, _13, _14, _15, _16, _17, _18, _19, _20, _21,
       _22, _23, _24, _25, _26, _27, _28, _29, _30, _31;

  Clock clock_1 (.out(clock_1_out));
  Multiplexer #(.select(5), .width(32)) multiplexer_1 (
    .in0({32{1'b0}}), .in1(_1), .in2(_2), .in3(_3), .in4(_4), .in5(_5), .in6(_6), .in7(_7), .in8(_8),
    .in9(_9), .in10(_10), .in11(_11), .in12(_12), .in13(_13), .in14(_14), .in15(_15), .in16(_16), .in17(_17),
    .in18(_18), .in19(_19), .in20(_20), .in21(_21), .in22(_22), .in23(_23), .in24(_24), .in25(_25),
    .in26(_26), .in27(_27), .in28(_28), .in29(_29), .in30(_30), .in31(_31), .out(RD1), .sel(Rs));  // open: en
  Register #(.width(32)) register_1 (.D(WD), .en(w1), .Q(_1), .clk(clock_1_out), .clr(reset));
  Register #(.width(32)) register_2 (.D(WD), .en(w8), .Q(_8), .clk(clock_1_out), .clr(reset));
  Register #(.width(32)) register_3 (.D(WD), .en(w9), .Q(_9), .clk(clock_1_out), .clr(reset));
  Register #(.width(32)) register_4 (.D(WD), .en(w17), .Q(_17), .clk(clock_1_out), .clr(reset));
  Register #(.width(32)) register_5 (.D(WD), .en(w16), .Q(_16), .clk(clock_1_out), .clr(reset));
  Register #(.width(32)) register_6 (.D(WD), .en(w24), .Q(_24), .clk(clock_1_out), .clr(reset));
  Register #(.width(32)) register_7 (.D(WD), .en(w25), .Q(_25), .clk(clock_1_out), .clr(reset));
  Register #(.width(32)) register_8 (.D(WD), .en(w2), .Q(_2), .clk(clock_1_out), .clr(reset));
  Register #(.width(32)) register_9 (.D(WD), .en(w10), .Q(_10), .clk(clock_1_out), .clr(reset));
  Register #(.width(32)) register_10 (.D(WD), .en(w18), .Q(_18), .clk(clock_1_out), .clr(reset));
  Register #(.width(32)) register_11 (.D(WD), .en(w26), .Q(_26), .clk(clock_1_out), .clr(reset));
  Multiplexer #(.select(5), .width(32)) multiplexer_2 (
    .in0({32{1'b0}}), .in1(_1), .in2(_2), .in3(_3), .in4(_4), .in5(_5), .in6(_6), .in7(_7), .in8(_8),
    .in9(_9), .in10(_10), .in11(_11), .in12(_12), .in13(_13), .in14(_14), .in15(_15), .in16(_16), .in17(_17),
    .in18(_18), .in19(_19), .in20(_20), .in21(_21), .in22(_22), .in23(_23), .in24(_24), .in25(_25),
    .in26(_26), .in27(_27), .in28(_28), .in29(_29), .in30(_30), .in31(_31), .out(RD2), .sel(Rt));  // open: en
  Register #(.width(32)) register_12 (.D(WD), .en(w3), .Q(_3), .clk(clock_1_out), .clr(reset));
  Register #(.width(32)) register_13 (.D(WD), .en(w11), .Q(_11), .clk(clock_1_out), .clr(reset));
  Register #(.width(32)) register_14 (.D(WD), .en(w19), .Q(_19), .clk(clock_1_out), .clr(reset));
  Register #(.width(32)) register_15 (.D(WD), .en(w27), .Q(_27), .clk(clock_1_out), .clr(reset));
  Register #(.width(32)) register_16 (.D(WD), .en(w4), .Q(_4), .clk(clock_1_out), .clr(reset));
  Register #(.width(32)) register_17 (.D(WD), .en(w12), .Q(_12), .clk(clock_1_out), .clr(reset));
  Register #(.width(32)) register_18 (.D(WD), .en(w20), .Q(_20), .clk(clock_1_out), .clr(reset));
  Register #(.width(32)) register_19 (.D(WD), .en(w28), .Q(_28), .clk(clock_1_out), .clr(reset));
  Demultiplexer #(.select(5)) demultiplexer_1 (
    .out1(w1), .out2(w2), .out3(w3), .out4(w4), .out5(w5), .out6(w6), .out7(w7), .out8(w8), .out9(w9),
    .out10(w10), .out11(w11), .out12(w12), .out13(w13), .out14(w14), .out15(w15), .out16(w16), .out17(w17),
    .out18(w18), .out19(w19), .out20(w20), .out21(w21), .out22(w22), .out23(w23), .out24(w24), .out25(w25),
    .out26(w26), .out27(w27), .out28(w28), .out29(w29), .out30(w30), .out31(w31), .in(Wr), .sel(Wt));  // open: out0, en
  Register #(.width(32)) register_20 (.D(WD), .en(w5), .Q(_5), .clk(clock_1_out), .clr(reset));
  Register #(.width(32)) register_21 (.D(WD), .en(w13), .Q(_13), .clk(clock_1_out), .clr(reset));
  Register #(.width(32)) register_22 (.D(WD), .en(w21), .Q(_21), .clk(clock_1_out), .clr(reset));
  Register #(.width(32)) register_23 (.D(WD), .en(w29), .Q(_29), .clk(clock_1_out), .clr(reset));
  Register #(.width(32)) register_24 (.D(WD), .en(w6), .Q(_6), .clk(clock_1_out), .clr(reset));
  Register #(.width(32)) register_25 (.D(WD), .en(w14), .Q(_14), .clk(clock_1_out), .clr(reset));
  Register #(.width(32)) register_26 (.D(WD), .en(w22), .Q(_22), .clk(clock_1_out), .clr(reset));
  Register #(.width(32)) register_27 (.D(WD), .en(w30), .Q(_30), .clk(clock_1_out), .clr(reset));
  Register #(.width(32)) register_28 (.D(WD), .en(w7), .Q(_7), .clk(clock_1_out), .clr(reset));
  Register #(.width(32)) register_29 (.D(WD), .en(w15), .Q(_15), .clk(clock_1_out), .clr(reset));
  Register #(.width(32)) register_30 (.D(WD), .en(w23), .Q(_23), .clk(clock_1_out), .clr(reset));
  Register #(.width(32)) register_31 (.D(WD), .en(w31), .Q(_31), .clk(clock_1_out), .clr(reset));

  // Other names for the same wires on the sheet: A1[4:0] = Rs; A2[4:0] = Rt; A3[4:0] = Wt; w[31:0] = WD
endmodule

module ALU (
  input  [31:0] A,
  input  [31:0] B,
  input  [1:0] ALUOp,
  output [31:0] C,
  output isZero
);

  wire [31:0] adder_1_out, or_1_out, subtractor_1_out;

  Adder #(.width(32)) adder_1 (.a(A), .b(B), .out(adder_1_out));  // open: cin, cout
  Subtractor #(.width(32)) subtractor_1 (.a(A), .b(B), .out(subtractor_1_out));  // open: bin, bout
  assign or_1_out = A | B;  // OR_Gate or_1, 32 bits wide
  Comparator #(.width(32)) comparator_1 (.a(A), .b(B), .eq(isZero));  // open: gt, lt
  Multiplexer #(.select(2), .width(32)) multiplexer_1 (
    .in0(adder_1_out), .in1(subtractor_1_out), .in2(or_1_out), .in3({32{1'b0}}), .out(C), .sel(ALUOp));  // open: en
endmodule

module DM (
  input  [31:0] Ad,
  input  [31:0] Wd,
  input  Reset,
  input  Wr,
  output [31:0] Rd
);

  wire clock_1_out;

  Clock clock_1 (.out(clock_1_out));
  RAM #(.addrWidth(12), .dataWidth(32), .bus("separate")) ram_1 (
    .addr(Ad[13:2]), .din(Wd), .data(Rd), .str(Wr), .clk(clock_1_out), .clr(Reset));  // open: sel, ld
endmodule

module EXT (
  input  [15:0] imm,
  input  [1:0] EXTOp,
  output [31:0] out
);

  wire [31:0] bit_extender_1_out, bit_extender_2_out;

  assign bit_extender_1_out = {{16{1'b0}}, imm};  // Bit_Extender bit_extender_1
  assign bit_extender_2_out = {{16{imm[15]}}, imm};  // Bit_Extender bit_extender_2
  Multiplexer #(.select(2), .width(32)) multiplexer_1 (
    .in0(bit_extender_1_out), .in1(bit_extender_2_out), .in2({imm, {16{1'b0}}}), .in3({32{1'b0}}), .out(out),
    .sel(EXTOp));  // open: en
endmodule

module OP (
  input  [5:0] Op,
  input  [5:0] funct,
  output ori,
  output \and ,
  output lw,
  output sub,
  output sw,
  output beq,
  output lui
);

  wire not_1_out, not_2_out, not_3_out, not_4_out, not_5_out, not_6_out, not_7_out, not_8_out, not_9_out,
       not_10_out, not_11_out, not_12_out, R;

  not not_1 (not_1_out, Op[0]);
  not not_2 (not_2_out, Op[1]);
  not not_3 (not_3_out, Op[3]);
  not not_4 (not_4_out, Op[2]);
  not not_5 (not_5_out, Op[5]);
  not not_6 (not_6_out, Op[4]);
  and and_1 (ori, not_5_out, not_6_out, Op[3], Op[2], not_2_out, Op[0]);
  and and_2 (lw, Op[5], not_6_out, not_3_out, not_4_out, Op[1], Op[0]);
  and and_3 (sw, Op[5], not_6_out, Op[3], not_4_out, Op[1], Op[0]);
  and and_4 (beq, not_5_out, not_6_out, not_3_out, Op[2], not_2_out, not_1_out);
  and and_5 (lui, not_5_out, not_6_out, Op[3], Op[2], Op[1], Op[0]);
  and and_6 (R, not_5_out, not_6_out, not_3_out, not_4_out, not_2_out, not_1_out);
  not not_7 (not_7_out, funct[0]);
  not not_8 (not_8_out, funct[1]);
  not not_9 (not_9_out, funct[2]);
  not not_10 (not_10_out, funct[4]);
  not not_11 (not_11_out, funct[3]);
  not not_12 (not_12_out, funct[5]);
  and and_7 (\and , funct[5], not_10_out, not_11_out, not_9_out, not_8_out, not_7_out, R);
  and and_8 (sub, funct[5], not_10_out, not_11_out, not_9_out, funct[1], not_7_out, R);
endmodule

module CTL (
  input  add,
  input  sub,
  input  ori,
  input  lw,
  input  sw,
  input  beq,
  input  lui,
  output NPCOp,
  output [1:0] EXTOp,
  output [1:0] ALUOp,
  output GRFWr,
  output DMWr,
  output M1Sel,
  output [1:0] M2Sel,
  output M3Sel
);

  wire not_1_out, not_2_out, not_3_out, not_4_out, not_5_out, not_6_out, not_7_out;

  not not_1 (not_1_out, add);
  not not_2 (not_2_out, ori);
  not not_3 (not_3_out, sub);
  not not_4 (not_4_out, lw);
  not not_5 (not_5_out, sw);
  not not_6 (not_6_out, lui);
  not not_7 (not_7_out, beq);
  or or_1 (EXTOp[0], sw, lw);
  and and_1 (GRFWr, not_5_out, not_7_out);
  or or_2 (M1Sel, add, sub);
  or or_3 (M3Sel, sw, lw, ori);

  assign ALUOp = {ori, sub};
  assign DMWr = sw;
  assign EXTOp[1] = lui;
  assign M2Sel = {lui, lw};
  assign NPCOp = beq;
endmodule

module Controller (
  input  [5:0] Opcode,
  input  [5:0] Funct,
  output NPCOp,
  output [1:0] EXTOp,
  output [1:0] ALUOp,
  output GRFWr,
  output DMWr,
  output M1Sel,
  output [1:0] M2Sel,
  output M3Sel
);

  wire op_1_and, op_1_beq, op_1_lui, op_1_lw, op_1_ori, op_1_sub, op_1_sw;

  OP op_1 (
    .Op(Opcode), .funct(Funct), .ori(op_1_ori), .\and (op_1_and), .lw(op_1_lw), .sub(op_1_sub), .sw(op_1_sw),
    .beq(op_1_beq), .lui(op_1_lui));
  CTL ctl_1 (
    .NPCOp(NPCOp), .EXTOp(EXTOp), .ALUOp(ALUOp), .GRFWr(GRFWr), .DMWr(DMWr), .M1Sel(M1Sel), .M2Sel(M2Sel),
    .M3Sel(M3Sel), .add(op_1_and), .sub(op_1_sub), .ori(op_1_ori), .lw(op_1_lw), .sw(op_1_sw),
    .beq(op_1_beq), .lui(op_1_lui));
endmodule

module main (
  input  reset,
  output [31:0] Instr,
  output [31:0] pc,
  output RegWrite,
  output [4:0] RegAddr,
  output [31:0] RegData,
  output MemWrite,
  output [31:0] MemAddr,
  output [31:0] MemData
);

  wire controller_1_m1sel, controller_1_m3sel, isZero, NPCOp;
  wire [1:0] controller_1_aluop, controller_1_m2sel, EXTOp;
  wire [4:0] splitter_1_rd, splitter_1_rs, splitter_1_rt;
  wire [5:0] splitter_1_funct, splitter_1_opcode;
  wire [15:0] splitter_1_imm;
  wire [31:0] DMOut, EXTOut, grf_1_rd1, multiplexer_3_out;

  IFU ifu_1 (.Reset(reset), .Instr(Instr), .isZero(isZero), .imm(splitter_1_imm), .pc(pc), .NPCOp(NPCOp));
  Splitter splitter_1 (
    .Instr(Instr), .Funct(splitter_1_funct), .Imm(splitter_1_imm), .Rd(splitter_1_rd), .Rt(splitter_1_rt),
    .Rs(splitter_1_rs), .Opcode(splitter_1_opcode));
  Controller controller_1 (
    .Opcode(splitter_1_opcode), .Funct(splitter_1_funct), .NPCOp(NPCOp), .EXTOp(EXTOp),
    .ALUOp(controller_1_aluop), .GRFWr(RegWrite), .DMWr(MemWrite), .M1Sel(controller_1_m1sel),
    .M2Sel(controller_1_m2sel), .M3Sel(controller_1_m3sel));
  Multiplexer #(.width(5)) multiplexer_1 (
    .in0(splitter_1_rt), .in1(splitter_1_rd), .out(RegAddr), .sel(controller_1_m1sel));  // open: en
  Multiplexer #(.select(2), .width(32)) multiplexer_2 (
    .in0(MemAddr), .in1(DMOut), .in2(EXTOut), .in3({32{1'b0}}), .out(RegData), .sel(controller_1_m2sel));  // open: en
  EXT ext_1 (.imm(splitter_1_imm), .EXTOp(EXTOp), .out(EXTOut));
  GRF grf_1 (
    .Rs(splitter_1_rs), .Rt(splitter_1_rt), .Wt(RegAddr), .WD(RegData), .RD1(grf_1_rd1), .RD2(MemData),
    .reset(reset), .Wr(RegWrite));
  Multiplexer #(.width(32)) multiplexer_3 (
    .in0(MemData), .in1(EXTOut), .out(multiplexer_3_out), .sel(controller_1_m3sel));  // open: en
  ALU alu_1 (.A(grf_1_rd1), .B(multiplexer_3_out), .ALUOp(controller_1_aluop), .C(MemAddr), .isZero(isZero));
  DM dm_1 (.Ad(MemAddr), .Wd(MemData), .Reset(reset), .Wr(MemWrite), .Rd(DMOut));

  // Other names for the same wires on the sheet: ALUOut[31:0] = MemAddr
endmodule

module Splitter (
  input  [31:0] Instr,
  output [5:0] Funct,
  output [15:0] Imm,
  output [4:0] Rd,
  output [4:0] Rt,
  output [4:0] Rs,
  output [5:0] Opcode
);


  assign Funct = Instr[5:0];
  assign Imm = Instr[15:0];
  assign Opcode = Instr[31:26];
  assign Rd = Instr[15:11];
  assign Rs = Instr[25:21];
  assign Rt = Instr[20:16];
endmodule
