// Logisim project cpu_test.circ as structural Verilog: 1 circuit, main circuit main
module main (
  output [31:0] Instr,
  output [31:0] pc,
  output RegWrite,
  output halt,
  output [4:0] RegAddr,
  output [31:0] RegData,
  output MemWrite,
  output [31:0] MemAddr,
  output [31:0] MemData
);

  wire clock_1_out, comparator_1_gt;
  wire [15:0] counter_1_q;

  Counter #(.width(16), .max('hffff)) counter_1 (
    .Q(counter_1_q), .carry(halt), .clk(clock_1_out));  // open: load, D, count, clr
  Clock clock_1 (.out(clock_1_out));
  cpu_main main_1 (
    .reset(comparator_1_gt), .Instr(Instr), .pc(pc), .RegWrite(RegWrite), .RegAddr(RegAddr),
    .RegData(RegData), .MemWrite(MemWrite), .MemAddr(MemAddr), .MemData(MemData));
  Comparator #(.width(16)) comparator_1 (.a(16'h4), .b(counter_1_q), .gt(comparator_1_gt));  // open: eq, lt
endmodule
